// Logisim project Clock_110.circ as structural Verilog: 1 circuit, main circuit clock
module clock (
  input  clock_auto,
  input  Select,
  input  clock_man,
  input  Hlt,
  output Clock,
  output nClock
);

  wire nand_1_out, nand_2_out, nand_3_out, not_1_out, not_2_out, not_3_out, not_4_out;

  not not_1 (not_1_out, not_2_out);
  not not_2 (not_2_out, Select);
  nand nand_1 (nand_1_out, clock_auto, not_1_out);
  not not_3 (not_3_out, not_1_out);
  not not_4 (not_4_out, Hlt);
  nand nand_2 (nand_2_out, not_3_out, clock_man);
  nand nand_3 (nand_3_out, nand_1_out, nand_2_out);
  nand nand_4 (nClock, nand_3_out, not_4_out);
  not not_5 (Clock, nClock);
endmodule
